# Fritzing sketch TalkTimer (saved by Fritzing 0.9.0b)

parts:
  Part4 = Lilypad Arduino Board
  Part5 = LilyPad Coin Cell Battery Holder
  Part6 = LilyPad Button Board
  Lilypad_Vibe1 = Lilypad Vibe Motor

nets:
  GND: Part4.GND, Part5.-, Lilypad_Vibe1.GND
  N1: Part4.TX/D1, Lilypad_Vibe1.Supply
  N2: Part4.RX/D0, Part6.-
  N3: Part4.VCC, Part5.+, Part6.S
